// Logisim project Brainfunk.circ as structural Verilog: 1 circuit, main circuit Brainfunk_CPU
module Brainfunk_CPU (
);

  wire and_1_out, CLK, CLK_STOP, clock_1_out, comparator_1_eq, DATA_BYPASS, FIND0_OP, FIND0_PAUSE, HALT_OP,
       IO_OP, IO_RD, IO_WAIT, IO_WR, JE_OP, JMP_OP, JN_OP, keyboard_1_avail, MAR_WR, MEM_WR, MUL_OP,
       MUL_PC_PAUSE, MUL_REG_RD, MUL_REG_WR, multiplexer_2_out, nor_1_out, not_1_out, or_1_out, RST, t_ff_1_q;
  wire [0:0] rom_1_data;
  wire [3:0] INST_OP;
  wire [6:0] keyboard_1_data;
  wire [7:0] adder_4_out, bit_extender_3_out, INST_DATA8, MEM_RD_BUS, MUL_REG, multiplexer_4_out,
       multiplexer_5_out, multiplexer_6_out, multiplier_1_out;
  wire [11:0] INST_OFFSET12;
  wire [15:0] adder_2_out, adder_3_out, bit_extender_1_out, bit_extender_2_out, MAR_q, MEM_ADDR;
  wire [19:0] adder_1_out, CODE_ADDR, multiplexer_1_out;

  Button button_1 (.out(RST));
  Clock clock_1 (.out(clock_1_out));
  nand nand_1 (CLK, clock_1_out, CLK_STOP);
  Multiplexer #(.width(20)) multiplexer_1 (
    .in0(20'h1), .in1({INST_OFFSET12, INST_DATA8}), .out(multiplexer_1_out), .sel(multiplexer_2_out));
  Multiplexer multiplexer_2 (.in0(JE_OP), .in1(JN_OP), .out(multiplexer_2_out), .sel(not_1_out));
  not not_1 (not_1_out, comparator_1_eq);
  Comparator #(.mode("unsigned")) comparator_1 (.a(MEM_RD_BUS), .b({8{1'b0}}), .eq(comparator_1_eq));  // open: gt, lt
  Bit_Extender #(.in_width(20)) bit_extender_1 (.in({INST_OFFSET12, INST_DATA8}), .out(bit_extender_1_out));
  ROM #(.addrWidth(4)) rom_1 (
    .addr(INST_OP), .data({MUL_OP, FIND0_OP, HALT_OP, DATA_BYPASS, IO_OP, JMP_OP, MAR_WR, rom_1_data[0]}));
  Demultiplexer demultiplexer_1 (.out0(IO_RD), .out1(IO_WR), .in(IO_OP), .sel(INST_DATA8[0]));
  D_Flip_Flop d_ff_1 (.D(HALT_OP), .clk(CLK), .Qn(CLK_STOP), .reset(RST));  // open: Q, preset
  Adder #(.width(20)) adder_1 (.a(CODE_ADDR), .b(multiplexer_1_out), .out(adder_1_out), .cin(1'b0));  // open: cout
  Register #(.width(16)) MAR (.D(adder_2_out), .en(or_1_out), .clk(CLK), .Q(MAR_q), .clr(RST));
  Adder #(.width(16)) adder_2 (.a(MAR_q), .b(bit_extender_1_out), .out(adder_2_out), .cin(1'b0));  // open: cout
  or or_1 (or_1_out, MAR_WR, FIND0_PAUSE);
  and and_1 (and_1_out, IO_WAIT, IO_RD);
  and and_2 (FIND0_PAUSE, FIND0_OP, not_1_out);
  assign bit_extender_2_out = {{4{INST_OFFSET12[11]}}, INST_OFFSET12};  // Bit_Extender bit_extender_2
  Demultiplexer demultiplexer_2 (.out0(JE_OP), .out1(JN_OP), .in(JMP_OP), .sel(INST_OP[0]));
  Register #(.width(20)) PC (.D(adder_1_out), .en(nor_1_out), .clk(CLK), .Q(CODE_ADDR), .clr(RST));
  nor nor_1 (nor_1_out, and_1_out, FIND0_PAUSE, MUL_PC_PAUSE);
  Adder #(.width(16)) adder_3 (.a(MAR_q), .b(bit_extender_2_out), .out(adder_3_out), .cin(1'b0));  // open: cout
  or or_2 (MEM_WR, rom_1_data[0], MUL_REG_RD);
  Multiplexer #(.width(16)) multiplexer_3 (.in0(MAR_q), .in1(adder_3_out), .out(MEM_ADDR), .sel(MUL_REG_RD));
  T_Flip_Flop t_ff_1 (.T(MUL_OP), .clk(CLK), .Q(t_ff_1_q), .reset(RST));  // open: Qn, preset
  Demultiplexer demultiplexer_3 (.out0(MUL_REG_RD), .out1(MUL_REG_WR), .in(MUL_OP), .sel(MUL_PC_PAUSE));
  // Probe on CODE_ADDR
  ROM #(.addrWidth(20), .dataWidth(24)) CODE_ROM (.addr(CODE_ADDR), .data({INST_OP, INST_OFFSET12, INST_DATA8}));
  xor xor_1 (MUL_PC_PAUSE, MUL_OP, t_ff_1_q);
  Multiplexer #(.width(8)) multiplexer_4 (.in0(INST_DATA8), .in1(MUL_REG), .out(multiplexer_4_out), .sel(MUL_REG_RD));
  Keyboard keyboard_1 (.clk(CLK), .re(IO_RD), .clr(RST), .avail(keyboard_1_avail), .data(keyboard_1_data));
  // Probe on {INST_OP, INST_OFFSET12, INST_DATA8}
  Adder adder_4 (.a(MEM_RD_BUS), .b(multiplexer_4_out), .out(adder_4_out), .cin(1'b0));  // open: cout
  // Probe on {INST_OFFSET12, INST_DATA8}
  // Probe on INST_OP
  TTY #(.cols(80), .rows(25)) tty_1 (.data(MEM_RD_BUS[6:0]), .clk(CLK), .we(IO_WR), .clr(RST));
  Multiplexer #(.width(8)) multiplexer_5 (
    .in0(adder_4_out), .in1(multiplexer_4_out), .out(multiplexer_5_out), .sel(DATA_BYPASS));
  not not_2 (IO_WAIT, keyboard_1_avail);
  // Probe on INST_OFFSET12
  assign bit_extender_3_out = {{1{1'b0}}, keyboard_1_data};  // Bit_Extender bit_extender_3
  RAM #(.addrWidth(16), .clearpin("true"), .enables("line")) DATA_RAM (
    .addr(MEM_ADDR), .we(MEM_WR), .clk(CLK), .din(multiplexer_6_out), .dout(MEM_RD_BUS), .clr(RST));
  Multiplexer #(.width(8)) multiplexer_6 (
    .in0(multiplexer_5_out), .in1(bit_extender_3_out), .out(multiplexer_6_out), .sel(IO_RD));
  // Probe on INST_DATA8
  Multiplier multiplier_1 (.a(MEM_RD_BUS), .b(INST_DATA8), .out(multiplier_1_out), .cin({8{1'b0}}));  // open: cout
  Register MUL (.D(multiplier_1_out), .en(MUL_REG_WR), .clk(CLK), .Q(MUL_REG), .clr(RST));

  // Other names for the same wires on the sheet: INST_OFFSET20[19:0] = {INST_OFFSET12, INST_DATA8};
  //   NJE_JN = INST_OP[0]

  // Notes on the sheet:
  //   contents of rom_1 (hex, n*v repeats v):
  //   20 1 11 80 40 2 4 4 8 7*20
endmodule
